# Fritzing sketch MidiController (saved by Fritzing 0.9.3b)
breadboards: 1

parts:
  Arduino = Arduino Micro (Rev3)
  R1 = Rotary Potentiometer (Small) [maximum_resistance=10kΩ package=THT]
  R2 = Rotary Potentiometer (Small) [maximum_resistance=10kΩ package=THT]
  R3 = Rotary Potentiometer (Small) [maximum_resistance=10kΩ package=THT]
  U1 = SLIDER [package=slider]
  R4 = Resistor [tolerance=±5% resistance=220 package=THT]
  R5 = Resistor [tolerance=±5% resistance=220 package=THT]
  R6 = Resistor [tolerance=±5% resistance=220 package=THT]
  R7 = Resistor [tolerance=±5% resistance=220 package=THT]
  S1 = Pushbutton [package=THT]
  R8 = Resistor [tolerance=±5% resistance=10k package=THT]
  R9 = Resistor [tolerance=±5% resistance=10k package=THT]
  R10 = Resistor [tolerance=±5% resistance=10k package=THT]
  R11 = Resistor [tolerance=±5% resistance=10k package=THT]
  R12 = Resistor [tolerance=±5% resistance=10k package=THT]
  R13 = Resistor [tolerance=±5% resistance=10k package=THT]
  R14 = Resistor [tolerance=±5% resistance=10k package=THT]
  R15 = Resistor [tolerance=±5% resistance=10k package=THT]
  R16 = Resistor [tolerance=±5% resistance=10k package=THT]
  R17 = Resistor [tolerance=±5% resistance=10k package=THT]
  R18 = Resistor [tolerance=±5% resistance=10k package=THT]
  R8_-_R19 = Resistor [tolerance=±5% resistance=100k package=THT]
  LED1 = LED - 5mm [color="Green (555nm)" package="5 mm [THT]"]
  LED2 = LED - 5mm [color="Green (555nm)" package="5 mm [THT]"]
  LED3 = LED - 5mm [color="Green (555nm)" package="5 mm [THT]"]
  LED4 = LED - 5mm [color="Green (555nm)" package="5 mm [THT]"]
  LED5 = LED - 5mm [color="Green (555nm)" package="5 mm [THT]"]
  LED6 = LED - 5mm [color="Green (555nm)" package="5 mm [THT]"]
  LED7 = LED - 5mm [color="Green (555nm)" package="5 mm [THT]"]
  LED8 = LED - 5mm [color="Green (555nm)" package="5 mm [THT]"]
  LED9 = LED - 5mm [color="Green (555nm)" package="5 mm [THT]"]
  LED10 = LED - 5mm [color="Green (555nm)" package="5 mm [THT]"]
  LED11 = LED - 5mm [color="Green (555nm)" package="5 mm [THT]"]
  LED12 = LED - 5mm [color="Green (555nm)" package="5 mm [THT]"]
  S2 = Pushbutton [package=THT]
  S3 = Pushbutton [package=THT]
  S4 = Pushbutton [package=THT]
  S5 = Pushbutton [package=THT]
  S6 = Pushbutton [package=THT]
  S7 = Pushbutton [package=THT]
  S8 = Pushbutton [package=THT]
  S9 = Pushbutton [package=THT]
  S10 = Pushbutton [package=THT]
  S11 = Pushbutton [package=THT]
  S12 = Pushbutton [package=THT]
  R20-R31 = Resistor [tolerance=±5% resistance=220 package=THT]
  R20-R32 = Resistor [tolerance=±5% resistance=100k package=THT]
  R20-R33 = Resistor [tolerance=±5% resistance=100k package=THT]
  R20-R34 = Resistor [tolerance=±5% resistance=100k package=THT]
  R20-R35 = Resistor [tolerance=±5% resistance=100k package=THT]
  R20-R36 = Resistor [tolerance=±5% resistance=100k package=THT]
  R20-R37 = Resistor [tolerance=±5% resistance=100k package=THT]
  R20-R38 = Resistor [tolerance=±5% resistance=100k package=THT]
  R20-R39 = Resistor [tolerance=±5% resistance=100k package=THT]
  R20-R40 = Resistor [tolerance=±5% resistance=100k package=THT]
  R20-R41 = Resistor [tolerance=±5% resistance=100k package=THT]
  R20-R42 = Resistor [tolerance=±5% resistance=100k package=THT]

nets:
  N1: Arduino.GND, R4.Pin_0, R5.Pin_0, R6.Pin_0, R7.Pin_0, R8.Pin_1, R9.Pin_1, R10.Pin_1, R11.Pin_1, R12.Pin_1, R13.Pin_1, R14.Pin_1, R15.Pin_1, R16.Pin_1, R17.Pin_1, R18.Pin_1, R8_-_R19.Pin_1, LED1.cathode, LED2.cathode, LED3.cathode, LED4.cathode, LED5.cathode, LED6.cathode, LED7.cathode, LED8.cathode, LED9.cathode, LED10.cathode, LED11.cathode, LED12.cathode
  N2: Arduino.D2/SDA, R8.Pin_0, S11.leg0, R20-R42.Pin_1
  N3: Arduino.D3/SCL, R9.Pin_0, S12.leg0, R20-R41.Pin_1
  N4: Arduino.D4_PWM/A6, R10.Pin_0, S10.leg0, R20-R40.Pin_1
  N5: Arduino.D5_PWM, R11.Pin_0, S9.leg0, R20-R38.Pin_1
  N6: Arduino.D6_PWM/A7, R12.Pin_0, S8.leg0, R20-R39.Pin_1
  N7: Arduino.D7, R13.Pin_0, S5.leg0, R20-R36.Pin_1
  N8: Arduino.D8_PWM/A8, R14.Pin_0, S7.leg0, R20-R37.Pin_1
  N9: Arduino.D9_PWM/A9, R15.Pin_0, S6.leg0, R20-R35.Pin_1
  N10: Arduino.D10_PWM/A10, R16.Pin_0, S3.leg0, R20-R34.Pin_1
  N11: Arduino.D11_PWM, R17.Pin_0, S4.leg0, R20-R33.Pin_1
  N12: Arduino.D12_PWM/A11, R18.Pin_0, S2.leg0, R20-R32.Pin_1
  N13: Arduino.5V, R1.leg1, R2.leg1, R3.leg1, U1.A, S1.leg1, S2.leg1, S3.leg1, S4.leg1, S5.leg1, S6.leg1, S7.leg1, S8.leg1, S9.leg1, S10.leg1, S11.leg1, S12.leg1
  N14: Arduino.A4, U1.S
  N15: Arduino.A3, R3.wiper
  N16: Arduino.A2, R2.wiper
  N17: Arduino.A1, R1.wiper
  N18: Arduino.D13_PWM, S1.leg0, R8_-_R19.Pin_0, R20-R31.Pin_1
  N19: R1.leg2, R7.Pin_1
  N20: R2.leg2, R6.Pin_1
  N21: R3.leg2, R5.Pin_1
  N22: U1.E, R4.Pin_1
  N23: LED1.anode, R20-R31.Pin_0
  N24: LED2.anode, R20-R32.Pin_0
  N25: LED3.anode, R20-R34.Pin_0
  N26: LED4.anode, R20-R33.Pin_0
  N27: LED5.anode, R20-R37.Pin_0
  N28: LED6.anode, R20-R35.Pin_0
  N29: LED7.anode, R20-R39.Pin_0
  N30: LED8.anode, R20-R36.Pin_0
  N31: LED9.anode, R20-R40.Pin_0
  N32: LED10.anode, R20-R38.Pin_0
  N33: LED11.anode, R20-R42.Pin_0
  N34: LED12.anode, R20-R41.Pin_0
